# Fritzing sketch Shema-KB-KS-IG (saved by Fritzing 0.9.9b)

parts:
  M1 = bn-880- GPS-module
  RE1 = KY-040 Rotary encoder [package=THT]
  Part1 = Arduino Mega ADK (Rev3)
  IC1 = DIP - 8 pins [chip_label=IC package="DIP (Dual Inline) [THT]"]
  U8 = 24V / 12V to 5V 5A powermodule DC-DC step-down power supply converter [package=molex-1x6]
  U10 = TB6600
  U12 = M40 [package=1x40_offset]  # not connected
  S1 = Pushbutton Yellow
  S4 = Pushbutton Black
  S2 = Pushbutton Green
  S3 = Pushbutton Red
  S6 = Round Pushbutton
  M2 = Stepper Motor - Bipolar
  J1 = Piezo Speaker
  BAT1 = 12 battery [package=battery]
  R1 = Temperature Sensor (Thermistor) [thermistor_type=NTC package=THT]
  R2 = Resistor [tolerance=±5% resistance=220 package=THT]

nets:
  N1: M1.pin_1, Part1.D20/SDA
  GND: M1.pin_2, RE1.GND, Part1.GND, IC1.GND, S1.leg0, S4.leg0, S2.leg0, S3.leg0, J1.pin1, R2.Pin_0
  N2: M1.pin_3, Part1.D18/TX1
  N3: M1.pin_4, Part1.D19/RX1
  VCC: M1.pin_5, RE1.Vcc, Part1.5V, IC1.V+, U10.connector7, U10.connector9, U10.connector11, R1.pin_0
  N4: M1.pin_6, Part1.D21/SCL
  N5: RE1.SW, Part1.D5_PWM
  N6: RE1.DT, Part1.D6_PWM
  N7: RE1.CLK, Part1.D7_PWM
  N8: Part1.A4, R1.pin_1, R2.Pin_1
  N9: Part1.D17/RX2, IC1.D3
  N10: Part1.D16/TX2, U10.connector10
  N11: Part1.D15/RX3, U10.connector8
  N12: Part1.D14/TX3, U10.connector6
  N13: Part1.D13_PWM, IC1.D2
  N14: Part1.D12_PWM, IC1.D1
  N15: Part1.D11_PWM, S4.leg1
  N16: Part1.D10_PWM, S3.leg1
  N17: Part1.D9_PWM, S2.leg1
  N18: Part1.D8_PWM, S1.leg1
  N19: Part1.D2_PWM, IC1.D0
  N20: Part1.D3_PWM, J1.pin2
  N21: U8.VIN+, U10.connector4, S6.pin2
  N22: U8.VIN-, U10.connector5, BAT1.-
  N23: U10.connector0, M2.D
  N24: U10.connector1, M2.B
  N25: U10.connector2, M2.C
  N26: U10.connector3, M2.A
  N27: S6.pin1, BAT1.+

custom parts:
  bn-880- GPS-module: bn-880l GPS module. Chipset : 8030-KT Receiving Format : GPS,GLONASS,Galileo,BeiDou,QZSS and SBAS
  KY-040 Rotary encoder: KY-040 Rotary Encoder with switch on breakout borad from AZ Delivery
  DIP - 8 pins: A DIP stand-in part for whatever IC you want. With 8 pins on a 300mil dual inline package (DIP) footprint.
  24V / 12V to 5V 5A powermodule DC-DC step-down power supply converter: 1: Input voltage: DC 9V - 36V; 2: The output voltage: 5.2V / 5A / 25W 3: Output capability: 9 ~ 24V Input: Output 5.2V / 6A / 30W 24 ~ 32V Input: Output 5.2V / 5A / 25W 32 ~ 36V Input: Output 5.2V / 3.5A / 18W
  M40: 1x40 .1 header
  Pushbutton Yellow: A generic pushbutton.
  Pushbutton Black: A generic pushbutton.
  Pushbutton Green: A generic pushbutton.
  Pushbutton Red: A generic pushbutton.
  Round Pushbutton: A generic pushbutton.
  12 battery: 12V lead acid type battery, like the Husqvarna YTH2448 12V 35AH battery. This is the mini version 1/4 the size of the actual battery to be closer to typical breadboard parts (around 2in wide rathher than 7in). The pads in pcb are sized to accomidate up to 14ga wire (as these batterys will deliver high currents.)
